// Logisim project lab_5_cs23b1024_oct14.circ as structural Verilog: 1 circuit, main circuit main
module main (
  input  A3,
  input  A2,
  input  A1,
  input  A0,
  input  B3,
  input  B2,
  input  B1,
  input  B0,
  input  C,
  output out_10,
  output CA4,
  output out_12,
  output CA3,
  output out_14,
  output CA2,
  output out_16,
  output CA1
);

  wire and_1_out, and_2_out, and_3_out, and_4_out, G0_out, G1_out, G2_out, G3_out, P0_out, P0C0_out, P1_out,
       P1G0_out, P1P0C0_out, P2_out, P2G1_out, P2P1G0_out, P2P1P0C0_out, P3_out;

  xor P3 (P3_out, A3, B3);
  and G3 (G3_out, A3, B3);
  xor P2 (P2_out, A2, B2);
  and G2 (G2_out, A2, B2);
  xor P1 (P1_out, A1, B1);
  and G1 (G1_out, A1, B1);
  xor P0 (P0_out, A0, B0);
  and G0 (G0_out, A0, B0);
  and and_1 (and_1_out, P3_out, G2_out);
  and P0C0 (P0C0_out, P0_out, C);
  and P2G1 (P2G1_out, P2_out, G1_out);
  and P1G0 (P1G0_out, P1_out, G0_out);
  and P1P0C0 (P1P0C0_out, P1_out, P0_out, C);
  or C0 (CA1, G0_out, P0C0_out);
  and P2P1P0C0 (P2P1P0C0_out, P2_out, P1P0C0_out);
  and P2P1G0 (P2P1G0_out, P2_out, P1G0_out);
  or C2 (CA3, P2P1P0C0_out, P2G1_out, P2P1G0_out, G2_out);
  or C1 (CA2, P1G0_out, P1P0C0_out, G1_out);
  and and_2 (and_2_out, P3_out, P2P1P0C0_out);
  and and_3 (and_3_out, P3_out, P2G1_out);
  and and_4 (and_4_out, P3_out, P2P1G0_out);
  or C3 (CA4, and_1_out, and_2_out, and_3_out, and_4_out, G3_out);
  xor S3 (out_10, P3_out, CA3);
  xor S2 (out_12, P2_out, CA2);
  xor S1 (out_14, P1_out, CA1);
  xor S0 (out_16, P0_out, C);
endmodule
